// Logisim project Calculator.circ as structural Verilog: 6 circuits, main circuit Calculator
module Calculator (
  input  in_1,
  input  in_2,
  input  OPERATION,
  input  in_4,
  input  in_5,
  input  in_6,
  input  in_7,
  input  in_8
);

  wire a, b, c, d, divider_flag, e, f, g, negative, zero_flag;

  Implementation implementation_1 (
    .in_1(in_6), .in_2(in_5), .in_3(in_4), .in_4(OPERATION), .in_5(in_2), .in_6(in_1), .a(a), .b(b), .c(c),
    .d(d), .e(e), .f(f), .g(g), .N(negative), .zero_flag(zero_flag), .divider_flag(divider_flag),
    .in_7(in_7), .in_8(in_8));
  _7_Segment_Display u_7_segment_display_1 (.g(negative));  // open: f, a, b, e, d, c, dp
  _7_Segment_Display u_7_segment_display_2 (.g(g), .f(f), .a(a), .b(b), .e(e), .d(d), .c(c));  // open: dp
  LED led_1 (.in(negative));
  LED led_2 (.in(zero_flag));
  LED led_3 (.in(divider_flag));

  // Other names for the same wires on the sheet: A0 = in_6; A1 = in_5; B0 = OPERATION; B1 = in_2; N0 = in_4;
  //   N1 = in_1; op0 = in_8; op1 = in_7

  // Notes on the sheet:
  //   0         0      -->     Addition
  //   0         1      -->     Subtraction
  //   1         0      -->     Multiplication
  //   1        1      -->     Division
endmodule

// ALU
module Implementation (
  input  in_1,
  input  in_2,
  input  in_3,
  input  in_4,
  input  in_5,
  input  in_6,
  input  in_7,
  input  in_8,
  output a,
  output b,
  output c,
  output d,
  output e,
  output f,
  output g,
  output N,
  output zero_flag,
  output divider_flag
);

  wire _0_flg, div, div_flag, minus_op0, minus_op1, mult, N0_S, N_D, N_D_F, N_M, N_M_F, N_S, N_S_F, N_t, S0,
       S0_1, S0_D, S0_M, S0_S, S1, S1_1, S1_D, S1_M, S1_S, S2, S2_1, S2_M, S2_S, S3, S3_1, S3_M;

  xor xor_1 (N0_S, in_8, in_3);
  Addition addition_1 (
    .in_1(in_1), .in_2(in_2), .in_3(N0_S), .in_4(in_4), .in_5(in_5), .in_6(in_6), .out_7(S0_S), .out_8(S1_S),
    .out_9(S2_S), .out_10(N_S));
  Multiplication multiplication_1 (
    .in_1(in_1), .in_2(in_2), .in_3(in_3), .in_4(in_4), .in_5(in_5), .in_6(in_6), .S0(S0_M), .S1(S1_M),
    .S2(S2_M), .S3(S3_M), .N(N_M));
  Division division_1 (
    .in_1(in_1), .in_2(in_2), .in_3(in_3), .in_4(in_4), .in_5(in_5), .in_6(in_6), .S0(S0_D), .S1(S1_D),
    .zero_divider_flag(div_flag), .N(N_D));
  // _74157 74157_1: pin names not known; wires that end beside it: in_7, S0_S, S0_1, S0, S1_S, S1_1, S1, 1'b0, 1'b1, 1'b0, S2_S, S2_1, S2, 1'b0, S3_1, S3
  // _74157 74157_2: pin names not known; wires that end beside it: in_8, S0_M, S0_D, S0_1, S1_M, S1_D, S1_1, 1'b0, 1'b1, 1'b0, S2_M, 1'b0, S2_1, S3_M, 1'b0, S3_1
  // _744075 744075_1: pin names not known; wires that end beside it: S0, S1, 1'b0, 1'b1, S2, _0_flg, N_S_F, N_M_F, N_D_F, N_t
  // _7408 7408_1: pin names not known; wires that end beside it: in_7, in_8, div, in_7, minus_op0, mult, 1'b0, 1'b1, mult, N_M, N_M_F, div, N_D, N_D_F
  // _7404 7404_1: pin names not known; wires that end beside it: in_8, minus_op0, in_7, minus_op1, 1'b0, 1'b1
  // _7408 7408_2: pin names not known; wires that end beside it: div_flag, div, divider_flag, minus_op1, N_S, N_S_F, 1'b0, 1'b1, N_t, _0_flg, N, minus_op1, N_S, N_S_F
  not not_1 (zero_flag, _0_flg);
  // _7448 7448_1: pin names not known; wires that end beside it: S1, S2, 1'b1, 1'b1, 1'b1, S3, S0, 1'b0, 1'b1, f, g, a, b, c, d, e

  // Other names for the same wires on the sheet: A0 = in_1; A1 = in_2; B0 = in_4; B1 = in_5; N0 = in_3; N1 = in_6;
  //   N_F = N; op0 = in_8; op1 = in_7

  // Notes on the sheet:
  //   0    0      -->     Addition
  //   0    1      -->     Addition
  //   1    0      -->     Multiplication
  //   1    1      -->     Division
endmodule

module Multiplication (
  input  in_1,
  input  in_2,
  input  in_3,
  input  in_4,
  input  in_5,
  input  in_6,
  output S0,
  output S1,
  output S2,
  output S3,
  output N
);

  wire C1, S1_1, S1_2, S2_1;

  // _7408 7408_1: pin names not known; wires that end beside it: in_1, in_4, S0, in_2, in_4, S1_1, 1'b0, 1'b1, in_1, in_5, S1_2, in_2, in_5, S2_1
  // _7486 7486_1: pin names not known; wires that end beside it: S1_1, S1_2, S1, S2_1, C1, S2, 1'b0, 1'b1, in_3, in_6, N
  // _7408 7408_2: pin names not known; wires that end beside it: S1_1, S1_2, C1, C1, S2_1, S3, 1'b0, 1'b1

  // Other names for the same wires on the sheet: A0 = in_1; A1 = in_2; B0 = in_4; B1 = in_5; N0 = in_3; N1 = in_6
endmodule

module Division (
  input  in_1,
  input  in_2,
  input  in_3,
  input  in_4,
  input  in_5,
  input  in_6,
  output S0,
  output S1,
  output zero_divider_flag,
  output N
);

  wire minus_A0, minus_A1, minus_B0, minus_S0_1, S0_1, S0_2, S1_1, S1_2;

  // _7408 7408_1: pin names not known; wires that end beside it: in_1, in_5, S0_1, minus_S0_1, S0_2, S0, 1'b0, 1'b1, in_2, in_4, S0_2, in_2, in_1, S1_1
  // _7404 7404_1: pin names not known; wires that end beside it: in_1, minus_A0, S0_1, minus_S0_1, in_4, minus_B0, 1'b0, 1'b1, in_2, minus_A1
  // _7408 7408_2: pin names not known; wires that end beside it: S1_1, S1_2, S1, in_5, minus_B0, S1_2, 1'b0, 1'b1, minus_A0, minus_A1, zero_divider_flag

  assign N = in_6;

  // Other names for the same wires on the sheet: A0 = in_1; A1 = in_2; B0 = in_4; B1 = in_5; N0 = in_3; N1 = in_6;
  //   zero_divider = zero_divider_flag
endmodule

module Addition (
  input  in_1,
  input  in_2,
  input  in_3,
  input  in_4,
  input  in_5,
  input  in_6,
  output out_7,
  output out_8,
  output out_9,
  output out_10
);

  wire A0_F, A1_F, B0_F, B1_F, C0, C2, CTRL1, CTRL2, CTRL3, minus_C2, minus_CTRL3, minus_N0, minus_N1,
       minus_N_xor, N, N_xor, S0, S0_F, S1, S1_F;

  // _7408 7408_1: pin names not known; wires that end beside it: in_3, minus_N1, CTRL1, minus_N0, in_6, CTRL2, 1'b0, 1'b1, C0, minus_C2, CTRL3, minus_N_xor, C2, out_9
  // _7432 7432_1: pin names not known; wires that end beside it: CTRL2, CTRL1, C0, 1'b0, 1'b1, CTRL1, CTRL2, N_xor, CTRL3, N, out_10
  _4_Bit_Adder_7483 u_4_bit_adder_7483_1 (
    ._2__S3(C2), ._3__A3(1'b0), ._4__B3(1'b0), ._5__Vcc(1'b1), ._6__S2(S1), ._7__B2(B1_F), ._8__A2(A1_F),
    ._13__Cin(C0), ._12__GND(1'b0), ._11__B1(B0_F), ._10__A1(A0_F), ._9__S1(S0));  // open: _1__A4, _16__B4, _15__S4, _14__cout
  // _7404 7404_1: pin names not known; wires that end beside it: in_6, minus_N1, in_3, minus_N0, C2, minus_C2, 1'b0, 1'b1, CTRL3, minus_CTRL3, N_xor, minus_N_xor
  // _7486 7486_1: pin names not known; wires that end beside it: in_1, CTRL1, A0_F, in_2, CTRL1, A1_F, 1'b0, 1'b1, in_4, CTRL2, B0_F, in_5, CTRL2, B1_F
  // _7486 7486_2: pin names not known; wires that end beside it: S0, CTRL3, S0_F, S1, CTRL3, S1_F, 1'b0, 1'b1, in_3, in_6
  _4_Bit_Adder_7483 u_4_bit_adder_7483_2 (
    ._6__S2(out_8), ._7__B2(1'b0), ._8__A2(S1_F), ._13__Cin(CTRL3), ._12__GND(1'b0), ._11__B1(1'b0),
    ._10__A1(S0_F), ._9__S1(out_7));  // open: _1__A4, _2__S3, _3__A3, _4__B3, _5__Vcc, _16__B4, _15__S4, _14__cout
  and AND (N, in_6, in_3);

  // Other names for the same wires on the sheet: A0 = in_1; A1 = in_2; B0 = in_4; B1 = in_5; N0 = in_3; N1 = in_6;
  //   N_F = out_10; S0_FF = out_7; S1_FF = out_8; S2_FF = out_9
endmodule

// 7483
module _4_Bit_Adder_7483 (
  input  _1__A4,
  input  _16__B4,
  input  _3__A3,
  input  _4__B3,
  input  _13__Cin,
  input  _5__Vcc,
  input  _12__GND,
  input  _11__B1,
  input  _7__B2,
  input  _10__A1,
  input  _8__A2,
  output _2__S3,
  output _15__S4,
  output _14__cout,
  output _6__S2,
  output _9__S1
);

  wire and_1_out, and_2_out, and_3_out, and_4_out, and_5_out, and_6_out, and_7_out, and_8_out, and_9_out,
       and_10_out, and_11_out, and_12_out, and_13_out, and_14_out, nand_1_out, nand_2_out, nand_3_out,
       nand_4_out, nor_1_out, nor_2_out, nor_3_out, nor_4_out, nor_6_out, nor_7_out, nor_8_out, not_1_out,
       not_2_out, not_3_out, not_4_out, not_5_out, not_6_out;

  nand nand_1 (nand_1_out, _16__B4, _1__A4);
  nor nor_1 (nor_1_out, _16__B4, _1__A4);
  nand nand_2 (nand_2_out, _4__B3, _3__A3);
  nor nor_2 (nor_2_out, _4__B3, _3__A3);
  nand nand_3 (nand_3_out, _7__B2, _8__A2);
  nor nor_3 (nor_3_out, _7__B2, _8__A2);
  nand nand_4 (nand_4_out, _11__B1, _10__A1);
  nor nor_4 (nor_4_out, _11__B1, _10__A1);
  and and_1 (and_1_out, nor_2_out, nand_1_out);
  and and_2 (and_2_out, nor_3_out, nand_1_out, nand_2_out);
  and and_3 (and_3_out, nor_4_out, nand_1_out, nand_2_out, nand_3_out);
  and and_4 (and_4_out, nand_1_out, nand_2_out, nand_3_out, nand_4_out, not_2_out);
  not not_1 (not_1_out, nor_1_out);
  and and_5 (and_5_out, nor_3_out, nand_2_out);
  and and_6 (and_6_out, nor_4_out, nand_2_out, nand_3_out);
  and and_7 (and_7_out, nand_2_out, nand_3_out, nand_4_out, not_2_out);
  not not_2 (not_2_out, _13__Cin);
  not not_3 (not_3_out, nor_2_out);
  and and_8 (and_8_out, nor_4_out, nand_3_out);
  and and_9 (and_9_out, nand_3_out, nand_4_out, not_2_out);
  not not_4 (not_4_out, nor_3_out);
  and and_10 (and_10_out, nand_4_out, not_2_out);
  not not_5 (not_5_out, nor_4_out);
  not not_6 (not_6_out, not_2_out);
  nor nor_5 (_14__cout, nor_1_out, and_1_out, and_2_out, and_3_out, and_4_out);
  and and_11 (and_11_out, nand_1_out, not_1_out);
  and and_12 (and_12_out, nand_2_out, not_3_out);
  and and_13 (and_13_out, nand_3_out, not_4_out);
  and and_14 (and_14_out, nand_4_out, not_5_out);
  xor xor_1 (_15__S4, and_11_out, nor_6_out);
  nor nor_6 (nor_6_out, nor_2_out, and_5_out, and_6_out, and_7_out);
  xor xor_2 (_2__S3, and_12_out, nor_7_out);
  nor nor_7 (nor_7_out, nor_3_out, and_8_out, and_9_out);
  xor xor_3 (_6__S2, and_13_out, nor_8_out);
  nor nor_8 (nor_8_out, nor_4_out, and_10_out);
  xor xor_4 (_9__S1, and_14_out, not_6_out);

  // Notes on the sheet:
  //   7483: 4-bit full adder
endmodule
